// Digital circuit overture.dig as structural Verilog
module overture (
  input  C_0,
  input  C_1,
  input  C_2,
  input  [7:0] A_0,
  input  [7:0] B_0,
  input  clk,
  input  [7:0] Num_1,
  input  In_3,
  input  In_2,
  input  In_1,
  output [7:0] O_0,
  output Out_0
);

  wire and_5_out, and_6_out, and_7_out, and_8_out, and_9_out, and_10_out, and_11_out, and_25_out, and_26_out,
       and_27_out, and_28_out, and_29_out, and_30_out, and_31_out, and_32_out, and_33_out, and_34_out,
       and_35_out, and_36_out, and_37_out, and_38_out, and_39_out, and_40_out, and_41_out, and_42_out,
       and_43_out, and_44_out, and_45_out, and_46_out, and_47_out, and_49_out, and_50_out, and_51_out,
       and_52_out, and_59_out, and_60_out, and_61_out, and_62_out, and_63_out, and_64_out, and_65_out,
       and_66_out, and_68_out, and_69_out, and_70_out, and_71_out, and_73_out, and_74_out, and_75_out,
       and_76_out, and_119_out, and_120_out, and_121_out, and_122_out, and_123_out, and_124_out, and_125_out,
       and_126_out, and_131_out, and_132_out, and_133_out, and_134_out, and_135_out, and_136_out,
       and_137_out, and_141_out, and_142_out, and_143_out, and_144_out, and_145_out, and_146_out,
       and_147_out, and_148_out, and_149_out, and_150_out, and_151_out, and_152_out, and_153_out,
       and_154_out, and_155_out, and_156_out, and_157_out, and_158_out, and_159_out, and_160_out,
       and_161_out, and_162_out, and_163_out, and_164_out, and_165_out, and_166_out, and_167_out,
       and_168_out, and_169_out, and_170_out, and_171_out, and_172_out, and_173_out, and_174_out,
       and_175_out, and_176_out, and_177_out, and_178_out, and_179_out, and_180_out, and_181_out,
       and_182_out, and_183_out, and_184_out, and_185_out, and_186_out, and_187_out, and_188_out,
       and_189_out, and_190_out, and_191_out, and_192_out, and_193_out, and_194_out, and_195_out,
       and_197_out, and_198_out, and_199_out, and_200_out, and_201_out, and_202_out, and_203_out,
       and_204_out, and_205_out, and_206_out, and_207_out, and_208_out, and_209_out, and_210_out,
       and_211_out, and_212_out, and_213_out, and_214_out, and_215_out, and_216_out, and_217_out,
       and_218_out, and_219_out, and_220_out, and_221_out, and_222_out, and_223_out, and_224_out,
       and_225_out, and_226_out, and_227_out, and_228_out, and_229_out, and_230_out, and_231_out,
       dipswitch_1_out, dipswitch_2_out, dipswitch_3_out, dipswitch_4_out, nand_1_out, nand_2_out,
       nand_3_out, nand_4_out, nand_5_out, nand_6_out, nand_7_out, nand_8_out, nand_9_out, nand_10_out,
       nand_11_out, nand_12_out, nand_13_out, nand_14_out, nand_15_out, nand_16_out, nand_18_out,
       nand_20_out, nand_22_out, nand_24_out, nand_25_out, nand_26_out, nand_27_out, nand_28_out,
       nand_29_out, nand_30_out, nand_31_out, nand_32_out, nand_33_out, nand_34_out, nand_35_out,
       nand_36_out, nand_37_out, nand_38_out, nand_39_out, nand_40_out, nand_42_out, nand_44_out,
       nand_46_out, nand_48_out, nand_57_out, nand_58_out, nand_59_out, nand_60_out, nand_61_out,
       nand_62_out, nand_63_out, nand_64_out, nand_65_out, nand_66_out, nand_67_out, nand_68_out,
       nand_69_out, nand_70_out, nand_71_out, nand_72_out, nand_73_out, nand_74_out, nand_75_out,
       nand_76_out, nand_77_out, nand_78_out, nand_79_out, nand_80_out, nand_81_out, nand_82_out,
       nand_83_out, nand_84_out, nand_85_out, nand_86_out, nand_87_out, nand_88_out, nand_89_out,
       nand_90_out, nand_91_out, nand_92_out, nand_93_out, nand_94_out, nand_95_out, nand_96_out,
       nand_97_out, nand_98_out, nand_99_out, nand_100_out, nand_101_out, nand_102_out, nand_103_out,
       nand_104_out, nand_105_out, nand_106_out, nand_107_out, nand_108_out, nand_109_out, nand_110_out,
       nand_111_out, nand_112_out, nor_9_out, nor_10_out, nor_11_out, nor_12_out, nor_13_out, nor_14_out,
       nor_15_out, nor_16_out, nor_17_out, nor_18_out, nor_19_out, nor_20_out, nor_21_out, nor_22_out,
       nor_23_out, nor_24_out, nor_25_out, nor_26_out, nor_27_out, nor_28_out, nor_29_out, nor_30_out,
       nor_31_out, nor_32_out, nor_33_out, nor_34_out, not_1_out, not_2_out, not_3_out, not_4_out, not_5_out,
       not_6_out, not_7_out, not_8_out, not_9_out, not_10_out, not_11_out, not_12_out, not_13_out,
       not_14_out, not_15_out, not_16_out, not_17_out, not_18_out, not_19_out, not_20_out, not_21_out,
       not_22_out, not_23_out, not_24_out, not_25_out, not_26_out, not_27_out, not_28_out, not_29_out,
       not_30_out, not_31_out, not_32_out, not_33_out, not_34_out, notconnected_2_out, notconnected_3_out,
       notconnected_4_out, notconnected_5_out, notconnected_9_out, notconnected_14_out, notconnected_18_out,
       notconnected_19_out, notconnected_20_out, notconnected_21_out, or_9_out, or_10_out, or_11_out,
       or_12_out, or_13_out, or_14_out, or_15_out, or_16_out, or_17_out, or_18_out, or_19_out, or_20_out,
       or_21_out, or_22_out, or_23_out, or_25_out, or_26_out, or_34_out, or_35_out, or_36_out, or_37_out,
       or_38_out, or_39_out, or_40_out, or_41_out, or_43_out, or_84_out, or_85_out, or_86_out, or_87_out,
       or_88_out, or_89_out, or_90_out, or_91_out, or_92_out, or_93_out, or_94_out, or_95_out, or_96_out,
       or_97_out, or_98_out, or_99_out, xor_9_out, xor_10_out, xor_11_out, xor_12_out, xor_13_out,
       xor_14_out, xor_15_out, xor_16_out, xor_23_out, xor_24_out, xor_25_out, xor_26_out, xor_27_out,
       xor_28_out, xor_29_out, xor_30_out, xor_41_out, xor_42_out, xor_43_out, xor_44_out, xor_45_out,
       xor_46_out, xor_47_out, xor_48_out, xor_49_out, xor_50_out, xor_51_out, xor_52_out, xor_53_out,
       xor_54_out, xor_55_out, xor_56_out, xor_57_out, xor_58_out, xor_59_out, xor_60_out, xor_61_out,
       xor_62_out, xor_63_out, xor_64_out, xor_65_out, xor_66_out, xor_67_out, xor_68_out, xor_69_out,
       xor_70_out, xor_71_out, xor_72_out;
  wire [7:0] and_16_out, and_24_out, and_72_out, and_112_out, and_113_out, and_114_out, and_115_out,
       and_116_out, and_140_out, nand_47_out, nand_56_out, nor_8_out, notconnected_1_out, notconnected_6_out,
       notconnected_7_out, notconnected_8_out, notconnected_10_out, notconnected_11_out, notconnected_12_out,
       notconnected_13_out, notconnected_15_out, notconnected_16_out, notconnected_17_out, or_8_out,
       or_42_out, or_80_out, or_81_out, or_82_out, or_83_out, xor_8_out, xor_36_out, xor_40_out;

  DipSwitch dipswitch_1 (.out(dipswitch_1_out));
  and and_1 (and_16_out[0], dipswitch_1_out, 1'b0);
  and and_2 (and_16_out[1], dipswitch_1_out, 1'b0);
  and and_3 (and_16_out[2], dipswitch_1_out, 1'b0);
  // And and_4 has open pins: In_1=and_5_out, In_2=nand_47_out[7], out=open
  xor xor_1 (xor_8_out[7], nand_47_out[7], and_5_out);
  and and_5 (and_5_out, and_6_out, nand_47_out[6]);
  xor xor_2 (xor_8_out[6], nand_47_out[6], and_6_out);
  and and_6 (and_6_out, and_7_out, nand_47_out[5]);
  xor xor_3 (xor_8_out[5], nand_47_out[5], and_7_out);
  and and_7 (and_7_out, and_8_out, nand_47_out[4]);
  xor xor_4 (xor_8_out[4], nand_47_out[4], and_8_out);
  and and_8 (and_8_out, and_9_out, nand_47_out[3]);
  xor xor_5 (xor_8_out[3], nand_47_out[3], and_9_out);
  and and_9 (and_9_out, and_10_out, nand_47_out[2]);
  xor xor_6 (xor_8_out[2], nand_47_out[2], and_10_out);
  and and_10 (and_10_out, and_11_out, nand_47_out[1]);
  xor xor_7 (xor_8_out[1], nand_47_out[1], and_11_out);
  and and_11 (and_11_out, 1'b1, nand_47_out[0]);
  xor xor_8 (xor_8_out[0], nand_47_out[0], 1'b1);
  and and_12 (and_16_out[3], dipswitch_1_out, 1'b0);
  and and_13 (and_16_out[4], dipswitch_1_out, 1'b0);
  and and_14 (and_16_out[5], dipswitch_1_out, 1'b0);
  and and_15 (and_16_out[6], dipswitch_1_out, 1'b0);
  not not_1 (not_1_out, dipswitch_1_out);
  and and_16 (and_16_out[7], dipswitch_1_out, 1'b0);
  or or_1 (or_8_out[0], and_24_out[0], and_16_out[0]);
  or or_2 (or_8_out[1], and_24_out[1], and_16_out[1]);
  or or_3 (or_8_out[2], and_24_out[2], and_16_out[2]);
  and and_17 (and_24_out[0], not_1_out, xor_8_out[0]);
  and and_18 (and_24_out[1], not_1_out, xor_8_out[1]);
  and and_19 (and_24_out[2], not_1_out, xor_8_out[2]);
  and and_20 (and_24_out[3], not_1_out, xor_8_out[3]);
  and and_21 (and_24_out[4], not_1_out, xor_8_out[4]);
  and and_22 (and_24_out[5], not_1_out, xor_8_out[5]);
  and and_23 (and_24_out[6], not_1_out, xor_8_out[6]);
  and and_24 (and_24_out[7], not_1_out, xor_8_out[7]);
  or or_4 (or_8_out[3], and_24_out[3], and_16_out[3]);
  or or_5 (or_8_out[4], and_24_out[4], and_16_out[4]);
  or or_6 (or_8_out[5], and_24_out[5], and_16_out[5]);
  or or_7 (or_8_out[6], and_24_out[6], and_16_out[6]);
  or or_8 (or_8_out[7], and_24_out[7], and_16_out[7]);
  nand nand_1 (nand_1_out, nand_4_out, nand_2_out);
  nand nand_2 (nand_2_out, nand_1_out, clk);
  nand nand_3 (nand_3_out, nand_2_out, clk, nand_4_out);
  nand nand_4 (nand_4_out, nand_3_out, or_8_out[6]);
  nand nand_5 (nand_5_out, nand_8_out, nand_6_out);
  nand nand_6 (nand_6_out, nand_5_out, clk);
  nand nand_7 (nand_7_out, nand_6_out, clk, nand_8_out);
  nand nand_8 (nand_8_out, nand_7_out, or_8_out[4]);
  nand nand_9 (nand_9_out, nand_12_out, nand_10_out);
  nand nand_10 (nand_10_out, nand_9_out, clk);
  nand nand_11 (nand_11_out, nand_10_out, clk, nand_12_out);
  nand nand_12 (nand_12_out, nand_11_out, or_8_out[2]);
  nand nand_13 (nand_13_out, nand_16_out, nand_14_out);
  nand nand_14 (nand_14_out, nand_13_out, clk);
  nand nand_15 (nand_15_out, nand_14_out, clk, nand_16_out);
  nand nand_16 (nand_16_out, nand_15_out, or_8_out[0]);
  nand nand_17 (nand_47_out[6], nand_2_out, nand_18_out);
  nand nand_18 (nand_18_out, nand_47_out[6], nand_3_out);
  nand nand_19 (nand_47_out[4], nand_6_out, nand_20_out);
  nand nand_20 (nand_20_out, nand_47_out[4], nand_7_out);
  nand nand_21 (nand_47_out[2], nand_10_out, nand_22_out);
  nand nand_22 (nand_22_out, nand_47_out[2], nand_11_out);
  nand nand_23 (nand_47_out[0], nand_14_out, nand_24_out);
  nand nand_24 (nand_24_out, nand_47_out[0], nand_15_out);
  and and_25 (and_25_out, nand_47_out[6], 1'b0);
  and and_26 (and_26_out, nand_47_out[4], 1'b0);
  and and_27 (and_27_out, nand_47_out[2], 1'b0);
  and and_28 (and_28_out, nand_47_out[0], 1'b0);
  nand nand_25 (nand_25_out, nand_28_out, nand_26_out);
  nand nand_26 (nand_26_out, nand_25_out, clk);
  nand nand_27 (nand_27_out, nand_26_out, clk, nand_28_out);
  nand nand_28 (nand_28_out, nand_27_out, or_8_out[7]);
  nand nand_29 (nand_29_out, nand_32_out, nand_30_out);
  nand nand_30 (nand_30_out, nand_29_out, clk);
  nand nand_31 (nand_31_out, nand_30_out, clk, nand_32_out);
  nand nand_32 (nand_32_out, nand_31_out, or_8_out[5]);
  nand nand_33 (nand_33_out, nand_36_out, nand_34_out);
  nand nand_34 (nand_34_out, nand_33_out, clk);
  nand nand_35 (nand_35_out, nand_34_out, clk, nand_36_out);
  nand nand_36 (nand_36_out, nand_35_out, or_8_out[3]);
  nand nand_37 (nand_37_out, nand_40_out, nand_38_out);
  nand nand_38 (nand_38_out, nand_37_out, clk);
  nand nand_39 (nand_39_out, nand_38_out, clk, nand_40_out);
  nand nand_40 (nand_40_out, nand_39_out, or_8_out[1]);
  nand nand_41 (nand_47_out[7], nand_26_out, nand_42_out);
  nand nand_42 (nand_42_out, nand_47_out[7], nand_27_out);
  and and_29 (and_29_out, nand_47_out[7], 1'b0);
  nand nand_43 (nand_47_out[5], nand_30_out, nand_44_out);
  nand nand_44 (nand_44_out, nand_47_out[5], nand_31_out);
  and and_30 (and_30_out, nand_47_out[5], 1'b0);
  nand nand_45 (nand_47_out[3], nand_34_out, nand_46_out);
  nand nand_46 (nand_46_out, nand_47_out[3], nand_35_out);
  and and_31 (and_31_out, nand_47_out[3], 1'b0);
  nand nand_47 (nand_47_out[1], nand_38_out, nand_48_out);
  nand nand_48 (nand_48_out, nand_47_out[1], nand_39_out);
  and and_32 (and_32_out, nand_47_out[1], 1'b0);
  not not_2 (not_2_out, In_3);
  not not_3 (not_3_out, In_2);
  not not_4 (not_4_out, In_1);
  not not_5 (not_5_out, In_3);
  not not_6 (not_6_out, In_2);
  not not_7 (not_7_out, In_1);
  not not_8 (not_8_out, not_2_out);
  and and_33 (and_33_out, not_4_out, not_3_out);
  and and_34 (and_34_out, In_1, not_3_out);
  and and_35 (and_35_out, not_4_out, In_2);
  and and_36 (and_36_out, In_2, In_1);
  and and_37 (and_37_out, not_7_out, not_6_out);
  and and_38 (and_38_out, In_1, not_6_out);
  and and_39 (and_39_out, not_7_out, In_2);
  and and_40 (and_40_out, In_2, In_1);
  and and_41 (and_41_out, and_33_out, not_5_out);
  and and_42 (and_42_out, and_34_out, not_5_out);
  and and_43 (and_43_out, and_35_out, not_5_out);
  and and_44 (and_44_out, and_36_out, not_5_out);
  and and_45 (and_45_out, and_37_out, not_8_out);
  and and_46 (and_46_out, and_38_out, not_8_out);
  and and_47 (and_47_out, and_39_out, not_8_out);
  // And and_48 has open pins: In_1=and_40_out, In_2=not_8_out, out=open
  or or_9 (or_9_out, Num_1[7], Num_1[6]);
  or or_10 (or_10_out, Num_1[5], Num_1[4]);
  or or_11 (or_11_out, Num_1[3], Num_1[2]);
  or or_12 (or_12_out, Num_1[1], Num_1[0]);
  or or_13 (or_13_out, or_9_out, or_10_out);
  or or_14 (or_14_out, or_13_out, or_15_out);
  or or_15 (or_15_out, or_11_out, or_12_out);
  or or_16 (or_16_out, and_46_out, or_17_out);
  or or_17 (or_17_out, and_45_out, and_41_out);
  or or_18 (or_18_out, and_47_out, or_19_out);
  or or_19 (or_19_out, and_51_out, or_23_out);
  or or_20 (or_20_out, or_19_out, or_18_out);
  or or_21 (or_21_out, and_43_out, and_45_out);
  or or_22 (or_22_out, and_44_out, and_46_out);
  or or_23 (or_23_out, and_50_out, or_25_out);
  or or_24 (Out_0, or_26_out, or_20_out);
  not not_9 (not_9_out, or_14_out);
  not not_10 (not_10_out, Num_1[7]);
  or or_25 (or_25_out, and_49_out, and_52_out);
  or or_26 (or_26_out, or_25_out, or_23_out);
  and and_49 (and_49_out, or_16_out, not_9_out);
  and and_50 (and_50_out, or_14_out, and_42_out);
  and and_51 (and_51_out, or_21_out, not_10_out);
  and and_52 (and_52_out, Num_1[7], or_22_out);
  xor xor_9 (xor_9_out, B_0[7], and_132_out);
  xor xor_10 (xor_10_out, B_0[6], and_132_out);
  xor xor_11 (xor_11_out, B_0[5], and_132_out);
  xor xor_12 (xor_12_out, B_0[4], and_132_out);
  xor xor_13 (xor_13_out, B_0[3], and_132_out);
  xor xor_14 (xor_14_out, B_0[2], and_132_out);
  xor xor_15 (xor_15_out, B_0[1], and_132_out);
  xor xor_16 (xor_16_out, B_0[0], and_132_out);
  and and_53 (and_72_out[0], B_0[0], A_0[0]);
  nand nand_49 (nand_56_out[0], B_0[0], A_0[0]);
  or or_27 (or_42_out[0], B_0[0], A_0[0]);
  nor nor_1 (nor_8_out[0], B_0[0], A_0[0]);
  xor xor_17 (xor_36_out[0], B_0[0], A_0[0]);
  and and_54 (and_72_out[1], B_0[1], A_0[1]);
  nand nand_50 (nand_56_out[1], B_0[1], A_0[1]);
  or or_28 (or_42_out[1], B_0[1], A_0[1]);
  nor nor_2 (nor_8_out[1], B_0[1], A_0[1]);
  xor xor_18 (xor_36_out[1], B_0[1], A_0[1]);
  and and_55 (and_72_out[2], B_0[2], A_0[2]);
  nand nand_51 (nand_56_out[2], B_0[2], A_0[2]);
  or or_29 (or_42_out[2], B_0[2], A_0[2]);
  nor nor_3 (nor_8_out[2], B_0[2], A_0[2]);
  xor xor_19 (xor_36_out[2], B_0[2], A_0[2]);
  and and_56 (and_72_out[3], B_0[3], A_0[3]);
  and and_57 (and_72_out[4], B_0[4], A_0[4]);
  nand nand_52 (nand_56_out[3], B_0[3], A_0[3]);
  nand nand_53 (nand_56_out[4], B_0[4], A_0[4]);
  or or_30 (or_42_out[3], B_0[3], A_0[3]);
  or or_31 (or_42_out[4], B_0[4], A_0[4]);
  nor nor_4 (nor_8_out[3], B_0[3], A_0[3]);
  nor nor_5 (nor_8_out[4], B_0[4], A_0[4]);
  xor xor_20 (xor_36_out[3], B_0[3], A_0[3]);
  xor xor_21 (xor_36_out[4], B_0[4], A_0[4]);
  and and_58 (and_72_out[5], B_0[5], A_0[5]);
  nand nand_54 (nand_56_out[5], B_0[5], A_0[5]);
  or or_32 (or_42_out[5], B_0[5], A_0[5]);
  nor nor_6 (nor_8_out[5], B_0[5], A_0[5]);
  xor xor_22 (xor_36_out[5], B_0[5], A_0[5]);
  and and_59 (and_59_out, xor_9_out, A_0[7]);
  xor xor_23 (xor_23_out, A_0[7], xor_9_out);
  and and_60 (and_60_out, xor_10_out, A_0[6]);
  xor xor_24 (xor_24_out, A_0[6], xor_10_out);
  and and_61 (and_61_out, xor_11_out, A_0[5]);
  xor xor_25 (xor_25_out, A_0[5], xor_11_out);
  and and_62 (and_62_out, xor_12_out, A_0[4]);
  xor xor_26 (xor_26_out, A_0[4], xor_12_out);
  and and_63 (and_63_out, xor_13_out, A_0[3]);
  xor xor_27 (xor_27_out, A_0[3], xor_13_out);
  and and_64 (and_64_out, xor_14_out, A_0[2]);
  xor xor_28 (xor_28_out, A_0[2], xor_14_out);
  and and_65 (and_65_out, xor_15_out, A_0[1]);
  xor xor_29 (xor_29_out, A_0[1], xor_15_out);
  and and_66 (and_66_out, xor_16_out, A_0[0]);
  xor xor_30 (xor_30_out, A_0[0], xor_16_out);
  and and_67 (and_72_out[6], B_0[6], A_0[6]);
  nand nand_55 (nand_56_out[6], B_0[6], A_0[6]);
  or or_33 (or_42_out[6], B_0[6], A_0[6]);
  nor nor_7 (nor_8_out[6], B_0[6], A_0[6]);
  xor xor_31 (xor_36_out[6], B_0[6], A_0[6]);
  or or_34 (or_34_out, and_59_out, and_68_out);
  and and_68 (and_68_out, xor_23_out, or_35_out);
  xor xor_32 (xor_40_out[7], xor_23_out, or_35_out);
  or or_35 (or_35_out, and_60_out, and_69_out);
  and and_69 (and_69_out, xor_24_out, or_36_out);
  xor xor_33 (xor_40_out[6], xor_24_out, or_36_out);
  or or_36 (or_36_out, and_61_out, and_70_out);
  and and_70 (and_70_out, xor_25_out, or_37_out);
  xor xor_34 (xor_40_out[5], xor_25_out, or_37_out);
  or or_37 (or_37_out, and_62_out, and_71_out);
  and and_71 (and_71_out, xor_26_out, or_38_out);
  xor xor_35 (xor_40_out[4], xor_26_out, or_38_out);
  or or_38 (or_38_out, and_63_out, and_73_out);
  or or_39 (or_39_out, and_64_out, and_74_out);
  or or_40 (or_40_out, and_65_out, and_75_out);
  or or_41 (or_41_out, and_66_out, and_76_out);
  and and_72 (and_72_out[7], B_0[7], A_0[7]);
  nand nand_56 (nand_56_out[7], B_0[7], A_0[7]);
  or or_42 (or_42_out[7], B_0[7], A_0[7]);
  nor nor_8 (nor_8_out[7], B_0[7], A_0[7]);
  xor xor_36 (xor_36_out[7], B_0[7], A_0[7]);
  and and_73 (and_73_out, xor_27_out, or_39_out);
  xor xor_37 (xor_40_out[3], xor_27_out, or_39_out);
  and and_74 (and_74_out, xor_28_out, or_40_out);
  xor xor_38 (xor_40_out[2], xor_28_out, or_40_out);
  and and_75 (and_75_out, xor_29_out, or_41_out);
  xor xor_39 (xor_40_out[1], xor_29_out, or_41_out);
  and and_76 (and_76_out, xor_30_out, and_132_out);
  xor xor_40 (xor_40_out[0], xor_30_out, and_132_out);
  and and_77 (and_112_out[0], and_133_out, and_72_out[0]);
  and and_78 (and_112_out[1], and_133_out, and_72_out[1]);
  and and_79 (and_113_out[0], and_134_out, nand_56_out[0]);
  and and_80 (and_113_out[1], and_134_out, nand_56_out[1]);
  and and_81 (and_114_out[0], and_135_out, or_42_out[0]);
  and and_82 (and_114_out[1], and_135_out, or_42_out[1]);
  and and_83 (and_115_out[0], and_136_out, nor_8_out[0]);
  and and_84 (and_115_out[1], and_136_out, nor_8_out[1]);
  and and_85 (and_116_out[0], and_137_out, xor_36_out[0]);
  and and_86 (and_116_out[1], and_137_out, xor_36_out[1]);
  and and_87 (and_112_out[2], and_133_out, and_72_out[2]);
  and and_88 (and_113_out[2], and_134_out, nand_56_out[2]);
  and and_89 (and_114_out[2], and_135_out, or_42_out[2]);
  and and_90 (and_115_out[2], and_136_out, nor_8_out[2]);
  and and_91 (and_116_out[2], and_137_out, xor_36_out[2]);
  and and_92 (and_112_out[3], and_133_out, and_72_out[3]);
  and and_93 (and_113_out[3], and_134_out, nand_56_out[3]);
  and and_94 (and_114_out[3], and_135_out, or_42_out[3]);
  and and_95 (and_115_out[3], and_136_out, nor_8_out[3]);
  and and_96 (and_116_out[3], and_137_out, xor_36_out[3]);
  and and_97 (and_112_out[4], and_133_out, and_72_out[4]);
  and and_98 (and_112_out[5], and_133_out, and_72_out[5]);
  and and_99 (and_113_out[4], and_134_out, nand_56_out[4]);
  and and_100 (and_113_out[5], and_134_out, nand_56_out[5]);
  and and_101 (and_114_out[4], and_135_out, or_42_out[4]);
  and and_102 (and_114_out[5], and_135_out, or_42_out[5]);
  and and_103 (and_115_out[4], and_136_out, nor_8_out[4]);
  and and_104 (and_115_out[5], and_136_out, nor_8_out[5]);
  and and_105 (and_116_out[4], and_137_out, xor_36_out[4]);
  and and_106 (and_116_out[5], and_137_out, xor_36_out[5]);
  and and_107 (and_112_out[6], and_133_out, and_72_out[6]);
  and and_108 (and_113_out[6], and_134_out, nand_56_out[6]);
  and and_109 (and_114_out[6], and_135_out, or_42_out[6]);
  and and_110 (and_115_out[6], and_136_out, nor_8_out[6]);
  and and_111 (and_116_out[6], and_137_out, xor_36_out[6]);
  and and_112 (and_112_out[7], and_133_out, and_72_out[7]);
  and and_113 (and_113_out[7], and_134_out, nand_56_out[7]);
  and and_114 (and_114_out[7], and_135_out, or_42_out[7]);
  and and_115 (and_115_out[7], and_136_out, nor_8_out[7]);
  and and_116 (and_116_out[7], and_137_out, xor_36_out[7]);
  not not_11 (not_11_out, C_2);
  and and_117 (and_140_out[0], or_43_out, xor_40_out[0]);
  not not_12 (not_12_out, C_1);
  not not_13 (not_13_out, C_1);
  and and_118 (and_140_out[1], or_43_out, xor_40_out[1]);
  not not_14 (not_14_out, C_0);
  and and_119 (and_119_out, not_14_out, not_12_out);
  and and_120 (and_120_out, C_0, not_12_out);
  and and_121 (and_121_out, not_14_out, C_1);
  and and_122 (and_122_out, C_1, C_0);
  not not_15 (not_15_out, C_2);
  not not_16 (not_16_out, C_0);
  and and_123 (and_123_out, not_16_out, not_13_out);
  and and_124 (and_124_out, C_0, not_13_out);
  and and_125 (and_125_out, not_16_out, C_1);
  and and_126 (and_126_out, C_1, C_0);
  not not_17 (not_17_out, not_11_out);
  and and_127 (and_140_out[2], or_43_out, xor_40_out[2]);
  and and_128 (and_140_out[3], or_43_out, xor_40_out[3]);
  and and_129 (and_140_out[4], or_43_out, xor_40_out[4]);
  // And and_130 has open pins: In_1=and_119_out, In_2=not_15_out, out=open
  and and_131 (and_131_out, and_120_out, not_15_out);
  and and_132 (and_132_out, and_121_out, not_15_out);
  and and_133 (and_133_out, and_122_out, not_15_out);
  and and_134 (and_134_out, and_123_out, not_17_out);
  and and_135 (and_135_out, and_124_out, not_17_out);
  and and_136 (and_136_out, and_125_out, not_17_out);
  and and_137 (and_137_out, and_126_out, not_17_out);
  and and_138 (and_140_out[5], or_43_out, xor_40_out[5]);
  and and_139 (and_140_out[6], or_43_out, xor_40_out[6]);
  and and_140 (and_140_out[7], or_43_out, xor_40_out[7]);
  or or_43 (or_43_out, and_131_out, and_132_out);
  or or_44 (O_0[0], and_140_out[0], or_80_out[0]);
  or or_45 (or_80_out[0], and_112_out[0], or_81_out[0]);
  or or_46 (or_81_out[0], and_113_out[0], or_82_out[0]);
  or or_47 (or_82_out[0], and_114_out[0], or_83_out[0]);
  or or_48 (or_83_out[0], and_115_out[0], and_116_out[0]);
  or or_49 (O_0[1], and_140_out[1], or_80_out[1]);
  or or_50 (or_80_out[1], and_112_out[1], or_81_out[1]);
  or or_51 (or_81_out[1], and_113_out[1], or_82_out[1]);
  or or_52 (or_82_out[1], and_114_out[1], or_83_out[1]);
  or or_53 (or_83_out[1], and_115_out[1], and_116_out[1]);
  or or_54 (O_0[2], and_140_out[2], or_80_out[2]);
  or or_55 (or_80_out[2], and_112_out[2], or_81_out[2]);
  or or_56 (or_81_out[2], and_113_out[2], or_82_out[2]);
  or or_57 (or_82_out[2], and_114_out[2], or_83_out[2]);
  or or_58 (or_83_out[2], and_115_out[2], and_116_out[2]);
  or or_59 (O_0[3], and_140_out[3], or_80_out[3]);
  or or_60 (O_0[4], and_140_out[4], or_80_out[4]);
  or or_61 (or_80_out[3], and_112_out[3], or_81_out[3]);
  or or_62 (or_80_out[4], and_112_out[4], or_81_out[4]);
  or or_63 (or_81_out[3], and_113_out[3], or_82_out[3]);
  or or_64 (or_81_out[4], and_113_out[4], or_82_out[4]);
  or or_65 (or_82_out[3], and_114_out[3], or_83_out[3]);
  or or_66 (or_82_out[4], and_114_out[4], or_83_out[4]);
  or or_67 (or_83_out[3], and_115_out[3], and_116_out[3]);
  or or_68 (or_83_out[4], and_115_out[4], and_116_out[4]);
  or or_69 (O_0[5], and_140_out[5], or_80_out[5]);
  or or_70 (or_80_out[5], and_112_out[5], or_81_out[5]);
  or or_71 (or_81_out[5], and_113_out[5], or_82_out[5]);
  or or_72 (or_82_out[5], and_114_out[5], or_83_out[5]);
  or or_73 (or_83_out[5], and_115_out[5], and_116_out[5]);
  or or_74 (O_0[6], and_140_out[6], or_80_out[6]);
  or or_75 (or_80_out[6], and_112_out[6], or_81_out[6]);
  or or_76 (or_81_out[6], and_113_out[6], or_82_out[6]);
  or or_77 (or_82_out[6], and_114_out[6], or_83_out[6]);
  or or_78 (or_83_out[6], and_115_out[6], and_116_out[6]);
  or or_79 (O_0[7], and_140_out[7], or_80_out[7]);
  or or_80 (or_80_out[7], and_112_out[7], or_81_out[7]);
  or or_81 (or_81_out[7], and_113_out[7], or_82_out[7]);
  or or_82 (or_82_out[7], and_114_out[7], or_83_out[7]);
  or or_83 (or_83_out[7], and_115_out[7], and_116_out[7]);
  // NotConnected on notconnected_1_out
  // NotConnected on notconnected_2_out
  // NotConnected on notconnected_3_out
  // NotConnected on notconnected_4_out
  // NotConnected on notconnected_5_out
  // NotConnected on notconnected_6_out
  // NotConnected on notconnected_7_out
  // NotConnected on notconnected_8_out
  nand nand_57 (nand_57_out, nand_60_out, nand_58_out);
  nand nand_58 (nand_58_out, nand_57_out, notconnected_2_out);
  nand nand_59 (nand_59_out, nand_58_out, notconnected_2_out, nand_60_out);
  nand nand_60 (nand_60_out, nand_59_out, notconnected_1_out[6]);
  nand nand_61 (nand_61_out, nand_64_out, nand_62_out);
  nand nand_62 (nand_62_out, nand_61_out, notconnected_2_out);
  nand nand_63 (nand_63_out, nand_62_out, notconnected_2_out, nand_64_out);
  nand nand_64 (nand_64_out, nand_63_out, notconnected_1_out[4]);
  nand nand_65 (nand_65_out, nand_68_out, nand_66_out);
  nand nand_66 (nand_66_out, nand_65_out, notconnected_2_out);
  nand nand_67 (nand_67_out, nand_66_out, notconnected_2_out, nand_68_out);
  nand nand_68 (nand_68_out, nand_67_out, notconnected_1_out[2]);
  nand nand_69 (nand_69_out, nand_72_out, nand_70_out);
  nand nand_70 (nand_70_out, nand_69_out, notconnected_2_out);
  nand nand_71 (nand_71_out, nand_70_out, notconnected_2_out, nand_72_out);
  nand nand_72 (nand_72_out, nand_71_out, notconnected_1_out[0]);
  DipSwitch dipswitch_2 (.out(dipswitch_2_out));
  DipSwitch dipswitch_3 (.out(dipswitch_3_out));
  DipSwitch dipswitch_4 (.out(dipswitch_4_out));
  not not_18 (not_18_out, notconnected_6_out[7]);
  and and_141 (and_141_out, notconnected_4_out, notconnected_6_out[7]);
  not not_19 (not_19_out, notconnected_6_out[6]);
  and and_142 (and_142_out, notconnected_4_out, notconnected_6_out[6]);
  not not_20 (not_20_out, notconnected_6_out[5]);
  and and_143 (and_143_out, notconnected_4_out, notconnected_6_out[5]);
  not not_21 (not_21_out, notconnected_6_out[4]);
  and and_144 (and_144_out, notconnected_4_out, notconnected_6_out[4]);
  not not_22 (not_22_out, notconnected_6_out[3]);
  and and_145 (and_145_out, notconnected_4_out, notconnected_6_out[3]);
  not not_23 (not_23_out, notconnected_6_out[2]);
  and and_146 (and_146_out, notconnected_4_out, notconnected_6_out[2]);
  not not_24 (not_24_out, notconnected_6_out[1]);
  and and_147 (and_147_out, notconnected_4_out, notconnected_6_out[1]);
  not not_25 (not_25_out, notconnected_6_out[0]);
  and and_148 (and_148_out, notconnected_4_out, notconnected_6_out[0]);
  and and_149 (and_149_out, not_26_out, dipswitch_3_out);
  not not_26 (not_26_out, dipswitch_4_out);
  and and_150 (and_150_out, dipswitch_3_out, dipswitch_4_out);
  and and_151 (and_151_out, not_18_out, notconnected_4_out);
  and and_152 (and_152_out, not_19_out, notconnected_4_out);
  and and_153 (and_153_out, not_20_out, notconnected_4_out);
  and and_154 (and_154_out, not_21_out, notconnected_4_out);
  and and_155 (and_155_out, not_22_out, notconnected_4_out);
  and and_156 (and_156_out, not_23_out, notconnected_4_out);
  and and_157 (and_157_out, not_24_out, notconnected_4_out);
  and and_158 (and_158_out, not_25_out, notconnected_4_out);
  nor nor_9 (nor_9_out, and_151_out, nor_10_out);
  nor nor_10 (nor_10_out, nor_9_out, and_141_out);
  nor nor_11 (nor_11_out, and_152_out, nor_12_out);
  nor nor_12 (nor_12_out, nor_11_out, and_142_out);
  nor nor_13 (nor_13_out, and_153_out, nor_14_out);
  nor nor_14 (nor_14_out, nor_13_out, and_143_out);
  nor nor_15 (nor_15_out, and_154_out, nor_16_out);
  nor nor_16 (nor_16_out, nor_15_out, and_144_out);
  nor nor_17 (nor_17_out, and_155_out, nor_18_out);
  nor nor_18 (nor_18_out, nor_17_out, and_145_out);
  nor nor_19 (nor_19_out, and_156_out, nor_20_out);
  nor nor_20 (nor_20_out, nor_19_out, and_146_out);
  nor nor_21 (nor_21_out, and_157_out, nor_22_out);
  nor nor_22 (nor_22_out, nor_21_out, and_147_out);
  nor nor_23 (nor_23_out, and_158_out, nor_24_out);
  nor nor_24 (nor_24_out, nor_23_out, and_148_out);
  nand nand_73 (nand_73_out, nand_58_out, nand_74_out);
  nand nand_74 (nand_74_out, nand_73_out, nand_59_out);
  and and_159 (and_159_out, nand_73_out, notconnected_3_out);
  nand nand_75 (nand_75_out, nand_62_out, nand_76_out);
  nand nand_76 (nand_76_out, nand_75_out, nand_63_out);
  and and_160 (and_160_out, nand_75_out, notconnected_3_out);
  nand nand_77 (nand_77_out, nand_66_out, nand_78_out);
  nand nand_78 (nand_78_out, nand_77_out, nand_67_out);
  and and_161 (and_161_out, nand_77_out, notconnected_3_out);
  nand nand_79 (nand_79_out, nand_70_out, nand_80_out);
  nand nand_80 (nand_80_out, nand_79_out, nand_71_out);
  and and_162 (and_162_out, nand_79_out, notconnected_3_out);
  and and_163 (and_163_out, notconnected_7_out[7], notconnected_8_out[7]);
  xor xor_41 (xor_41_out, notconnected_8_out[7], notconnected_7_out[7]);
  and and_164 (and_164_out, notconnected_7_out[6], notconnected_8_out[6]);
  xor xor_42 (xor_42_out, notconnected_8_out[6], notconnected_7_out[6]);
  and and_165 (and_165_out, notconnected_7_out[5], notconnected_8_out[5]);
  xor xor_43 (xor_43_out, notconnected_8_out[5], notconnected_7_out[5]);
  and and_166 (and_166_out, notconnected_7_out[4], notconnected_8_out[4]);
  xor xor_44 (xor_44_out, notconnected_8_out[4], notconnected_7_out[4]);
  and and_167 (and_167_out, notconnected_7_out[3], notconnected_8_out[3]);
  xor xor_45 (xor_45_out, notconnected_8_out[3], notconnected_7_out[3]);
  and and_168 (and_168_out, notconnected_7_out[2], notconnected_8_out[2]);
  xor xor_46 (xor_46_out, notconnected_8_out[2], notconnected_7_out[2]);
  and and_169 (and_169_out, notconnected_7_out[1], notconnected_8_out[1]);
  xor xor_47 (xor_47_out, notconnected_8_out[1], notconnected_7_out[1]);
  and and_170 (and_170_out, notconnected_7_out[0], notconnected_8_out[0]);
  xor xor_48 (xor_48_out, notconnected_8_out[0], notconnected_7_out[0]);
  nor nor_25 (nor_25_out, and_149_out, nor_26_out);
  nor nor_26 (nor_26_out, nor_25_out, and_150_out);
  or or_84 (or_84_out, and_163_out, and_171_out);
  and and_171 (and_171_out, xor_41_out, or_85_out);
  xor xor_49 (xor_49_out, xor_41_out, or_85_out);
  or or_85 (or_85_out, and_164_out, and_172_out);
  and and_172 (and_172_out, xor_42_out, or_86_out);
  xor xor_50 (xor_50_out, xor_42_out, or_86_out);
  or or_86 (or_86_out, and_165_out, and_173_out);
  and and_173 (and_173_out, xor_43_out, or_87_out);
  xor xor_51 (xor_51_out, xor_43_out, or_87_out);
  or or_87 (or_87_out, and_166_out, and_174_out);
  and and_174 (and_174_out, xor_44_out, or_88_out);
  xor xor_52 (xor_52_out, xor_44_out, or_88_out);
  or or_88 (or_88_out, and_167_out, and_183_out);
  or or_89 (or_89_out, and_168_out, and_184_out);
  or or_90 (or_90_out, and_169_out, and_185_out);
  or or_91 (or_91_out, and_170_out, and_186_out);
  // NotConnected on notconnected_9_out
  Reset reset_1 ();  // open: out
  Reset reset_2 ();  // open: out
  and and_175 (and_175_out, nor_9_out, notconnected_5_out);
  Reset reset_3 ();  // open: out
  and and_176 (and_176_out, nor_11_out, notconnected_5_out);
  Reset reset_4 ();  // open: out
  and and_177 (and_177_out, nor_13_out, notconnected_5_out);
  Reset reset_5 ();  // open: out
  and and_178 (and_178_out, nor_15_out, notconnected_5_out);
  Reset reset_6 ();  // open: out
  and and_179 (and_179_out, nor_17_out, notconnected_5_out);
  Reset reset_7 ();  // open: out
  and and_180 (and_180_out, nor_19_out, notconnected_5_out);
  Reset reset_8 ();  // open: out
  and and_181 (and_181_out, nor_21_out, notconnected_5_out);
  Reset reset_9 ();  // open: out
  and and_182 (and_182_out, nor_23_out, notconnected_5_out);
  and and_183 (and_183_out, xor_45_out, or_89_out);
  xor xor_53 (xor_53_out, xor_45_out, or_89_out);
  and and_184 (and_184_out, xor_46_out, or_90_out);
  xor xor_54 (xor_54_out, xor_46_out, or_90_out);
  and and_185 (and_185_out, xor_47_out, or_91_out);
  xor xor_55 (xor_55_out, xor_47_out, or_91_out);
  and and_186 (and_186_out, xor_48_out, notconnected_9_out);
  xor xor_56 (xor_56_out, xor_48_out, notconnected_9_out);
  and and_187 (and_187_out, nor_25_out, dipswitch_2_out);
  nand nand_81 (nand_81_out, nand_84_out, nand_82_out);
  nand nand_82 (nand_82_out, nand_81_out, notconnected_2_out);
  nand nand_83 (nand_83_out, nand_82_out, notconnected_2_out, nand_84_out);
  nand nand_84 (nand_84_out, nand_83_out, notconnected_1_out[7]);
  nand nand_85 (nand_85_out, nand_88_out, nand_86_out);
  nand nand_86 (nand_86_out, nand_85_out, notconnected_2_out);
  nand nand_87 (nand_87_out, nand_86_out, notconnected_2_out, nand_88_out);
  nand nand_88 (nand_88_out, nand_87_out, notconnected_1_out[5]);
  nand nand_89 (nand_89_out, nand_92_out, nand_90_out);
  nand nand_90 (nand_90_out, nand_89_out, notconnected_2_out);
  nand nand_91 (nand_91_out, nand_90_out, notconnected_2_out, nand_92_out);
  nand nand_92 (nand_92_out, nand_91_out, notconnected_1_out[3]);
  nand nand_93 (nand_93_out, nand_96_out, nand_94_out);
  nand nand_94 (nand_94_out, nand_93_out, notconnected_2_out);
  nand nand_95 (nand_95_out, nand_94_out, notconnected_2_out, nand_96_out);
  nand nand_96 (nand_96_out, nand_95_out, notconnected_1_out[1]);
  nand nand_97 (nand_97_out, nand_82_out, nand_98_out);
  nand nand_98 (nand_98_out, nand_97_out, nand_83_out);
  and and_188 (and_188_out, nand_97_out, notconnected_3_out);
  nand nand_99 (nand_99_out, nand_86_out, nand_100_out);
  nand nand_100 (nand_100_out, nand_99_out, nand_87_out);
  and and_189 (and_189_out, nand_99_out, notconnected_3_out);
  nand nand_101 (nand_101_out, nand_90_out, nand_102_out);
  nand nand_102 (nand_102_out, nand_101_out, nand_91_out);
  and and_190 (and_190_out, nand_101_out, notconnected_3_out);
  nand nand_103 (nand_103_out, nand_94_out, nand_104_out);
  nand nand_104 (nand_104_out, nand_103_out, nand_95_out);
  and and_191 (and_191_out, nand_103_out, notconnected_3_out);
  // NotConnected on notconnected_10_out
  // NotConnected on notconnected_11_out
  // NotConnected on notconnected_12_out
  // NotConnected on notconnected_13_out
  and and_192 (and_192_out, notconnected_11_out[0], notconnected_11_out[0]);
  or or_92 (or_92_out, notconnected_12_out[0], notconnected_12_out[0]);
  xor xor_57 (xor_57_out, notconnected_13_out[0], notconnected_13_out[0]);
  and and_193 (and_193_out, notconnected_11_out[1], notconnected_11_out[1]);
  or or_93 (or_93_out, notconnected_12_out[1], notconnected_12_out[1]);
  xor xor_58 (xor_58_out, notconnected_13_out[1], notconnected_13_out[1]);
  not not_27 (not_27_out, notconnected_14_out);
  // NotConnected on notconnected_14_out
  and and_194 (and_194_out, notconnected_11_out[2], notconnected_11_out[2]);
  and and_195 (and_195_out, notconnected_11_out[3], notconnected_11_out[3]);
  or or_94 (or_94_out, notconnected_12_out[2], notconnected_12_out[2]);
  or or_95 (or_95_out, notconnected_12_out[3], notconnected_12_out[3]);
  xor xor_59 (xor_59_out, notconnected_13_out[2], notconnected_13_out[2]);
  xor xor_60 (xor_60_out, notconnected_13_out[3], notconnected_13_out[3]);
  // And and_196 has open pins: In_1=and_197_out, In_2=notconnected_10_out[7], out=open
  xor xor_61 (xor_61_out, notconnected_10_out[7], and_197_out);
  and and_197 (and_197_out, and_198_out, notconnected_10_out[6]);
  xor xor_62 (xor_62_out, notconnected_10_out[6], and_198_out);
  and and_198 (and_198_out, and_199_out, notconnected_10_out[5]);
  xor xor_63 (xor_63_out, notconnected_10_out[5], and_199_out);
  and and_199 (and_199_out, and_200_out, notconnected_10_out[4]);
  xor xor_64 (xor_64_out, notconnected_10_out[4], and_200_out);
  and and_200 (and_200_out, and_201_out, notconnected_10_out[3]);
  xor xor_65 (xor_65_out, notconnected_10_out[3], and_201_out);
  and and_201 (and_201_out, and_202_out, notconnected_10_out[2]);
  xor xor_66 (xor_66_out, notconnected_10_out[2], and_202_out);
  and and_202 (and_202_out, and_203_out, notconnected_10_out[1]);
  xor xor_67 (xor_67_out, notconnected_10_out[1], and_203_out);
  and and_203 (and_203_out, not_27_out, notconnected_10_out[0]);
  xor xor_68 (xor_68_out, notconnected_10_out[0], not_27_out);
  and and_204 (and_204_out, notconnected_11_out[4], notconnected_11_out[4]);
  or or_96 (or_96_out, notconnected_12_out[4], notconnected_12_out[4]);
  xor xor_69 (xor_69_out, notconnected_13_out[4], notconnected_13_out[4]);
  and and_205 (and_205_out, notconnected_11_out[5], notconnected_11_out[5]);
  or or_97 (or_97_out, notconnected_12_out[5], notconnected_12_out[5]);
  xor xor_70 (xor_70_out, notconnected_13_out[5], notconnected_13_out[5]);
  and and_206 (and_206_out, notconnected_11_out[6], notconnected_11_out[6]);
  and and_207 (and_207_out, notconnected_11_out[7], notconnected_11_out[7]);
  or or_98 (or_98_out, notconnected_12_out[6], notconnected_12_out[6]);
  or or_99 (or_99_out, notconnected_12_out[7], notconnected_12_out[7]);
  xor xor_71 (xor_71_out, notconnected_13_out[6], notconnected_13_out[6]);
  xor xor_72 (xor_72_out, notconnected_13_out[7], notconnected_13_out[7]);
  // NotConnected on notconnected_15_out
  // NotConnected on notconnected_16_out
  // NotConnected on notconnected_17_out
  // NotConnected on notconnected_18_out
  // NotConnected on notconnected_19_out
  // NotConnected on notconnected_20_out
  and and_208 (and_208_out, notconnected_21_out, notconnected_15_out[0]);
  nand nand_105 (nand_105_out, notconnected_16_out[0], notconnected_16_out[0]);
  nor nor_27 (nor_27_out, notconnected_17_out[0], notconnected_17_out[0]);
  not not_28 (not_28_out, notconnected_20_out);
  and and_209 (and_209_out, notconnected_21_out, notconnected_15_out[1]);
  and and_210 (and_210_out, notconnected_21_out, notconnected_15_out[2]);
  nand nand_106 (nand_106_out, notconnected_16_out[1], notconnected_16_out[1]);
  nand nand_107 (nand_107_out, notconnected_16_out[2], notconnected_16_out[2]);
  nor nor_28 (nor_28_out, notconnected_17_out[1], notconnected_17_out[1]);
  nor nor_29 (nor_29_out, notconnected_17_out[2], notconnected_17_out[2]);
  not not_29 (not_29_out, notconnected_19_out);
  not not_30 (not_30_out, notconnected_18_out);
  not not_31 (not_31_out, notconnected_20_out);
  not not_32 (not_32_out, notconnected_19_out);
  not not_33 (not_33_out, notconnected_18_out);
  not not_34 (not_34_out, not_28_out);
  // NotConnected on notconnected_21_out
  and and_211 (and_211_out, notconnected_21_out, notconnected_15_out[3]);
  nand nand_108 (nand_108_out, notconnected_16_out[3], notconnected_16_out[3]);
  nor nor_30 (nor_30_out, notconnected_17_out[3], notconnected_17_out[3]);
  and and_212 (and_212_out, not_30_out, not_29_out);
  and and_213 (and_213_out, notconnected_18_out, not_29_out);
  and and_214 (and_214_out, not_30_out, notconnected_19_out);
  and and_215 (and_215_out, notconnected_19_out, notconnected_18_out);
  and and_216 (and_216_out, not_33_out, not_32_out);
  and and_217 (and_217_out, notconnected_18_out, not_32_out);
  and and_218 (and_218_out, not_33_out, notconnected_19_out);
  and and_219 (and_219_out, notconnected_19_out, notconnected_18_out);
  and and_220 (and_220_out, notconnected_21_out, notconnected_15_out[4]);
  nand nand_109 (nand_109_out, notconnected_16_out[4], notconnected_16_out[4]);
  nor nor_31 (nor_31_out, notconnected_17_out[4], notconnected_17_out[4]);
  and and_221 (and_221_out, and_212_out, not_31_out);
  and and_222 (and_222_out, and_213_out, not_31_out);
  and and_223 (and_223_out, and_214_out, not_31_out);
  and and_224 (and_224_out, and_215_out, not_31_out);
  and and_225 (and_225_out, and_216_out, not_34_out);
  and and_226 (and_226_out, and_217_out, not_34_out);
  and and_227 (and_227_out, and_218_out, not_34_out);
  and and_228 (and_228_out, and_219_out, not_34_out);
  and and_229 (and_229_out, notconnected_21_out, notconnected_15_out[5]);
  and and_230 (and_230_out, notconnected_21_out, notconnected_15_out[6]);
  nand nand_110 (nand_110_out, notconnected_16_out[5], notconnected_16_out[5]);
  nand nand_111 (nand_111_out, notconnected_16_out[6], notconnected_16_out[6]);
  nor nor_32 (nor_32_out, notconnected_17_out[5], notconnected_17_out[5]);
  nor nor_33 (nor_33_out, notconnected_17_out[6], notconnected_17_out[6]);
  and and_231 (and_231_out, notconnected_21_out, notconnected_15_out[7]);
  nand nand_112 (nand_112_out, notconnected_16_out[7], notconnected_16_out[7]);
  nor nor_34 (nor_34_out, notconnected_17_out[7], notconnected_17_out[7]);

  // Notes on the sheet:
  //   Overwrite Value
  //   Overwrite
  //   COUNTER
  //   B
  //   Select
  //   MUX
  //   A
  //   INCRMNT
  //   SWITCH
  //   OR
  //   Edge Flop
  //   D
  //   Clk
  //   Load
  //   Latch
  //   Always
  //   Loaded
  //   Conditional Unit
  //   3x8 Demux
  //   A1
  //   A2
  //   A3
  //   A_0
  //   2x4 Demux
  //   A_1
  //   Disable
  //   Is less than 0 Unit
  //   Is!0 Unit
  //   Is0
  //   IsNot0
  //   More
  //   Less
  //   MoreOrEqual
  //   LessOrEqual
  //   Never
  //   ALU
  //   ADDER
  //   AND
  //   NAND
  //   NOR
  //   XOR
  //   .
  //   COMPONENTS
  //   Register - outdated
  //   Save
  //   Save Value
  //   Edge Register
  //   1 Bit mem
  //   SaveVal
  //   Reset
  //   Write
  //   Always OUT
  //   OUT
  //   Always On Out
  //   Out
endmodule

/* Test case:
D C L ALWAYS LOADED
# 1. Randomized Startup: Register state is unknown (X). LOADED is 0 because L=0.
0x00 0 0 X 0x00

# 2. Load 0xAA: ALWAYS updates to 0xAA. LOADED shows it because L=1.
0xAA C 1 0xAA 0xAA

# 3. Transparent Check: ALWAYS stays 0xAA. LOADED drops to 0x00 because L=0.
0x55 0 0 0xAA 0x00
0x21 C 0 0x21 0x00

# 5. Load 0x00: Register becomes 0. Both pins show 0.
0x00 C 1 0x00 0x00

# 6. Edge-Triggering: Data 0xEE only moves to ALWAYS on the rising edge.
0xEE 0 1 0x00 0x00  # L=1, but no clock yet; LOADED is 0 because reg is 0
0xEE 1 1 0xEE 0xEE  # Clock goes high; Reg becomes 0xEE. LOADED now shows it.
0xDD 0 1 0xEE 0xEE  # Clock falls; Reg stays 0xEE.

# 7. High-Clock Stability Test
0xAA 0 1 0xEE 0xEE  # Prepare data 0xAA, but clock is 0. ALWAYS stays 0xEE.
0xAA 1 1 0xAA 0xAA  # Clock goes High. Register captures 0xAA.
0xFF 1 1 0xAA 0xAA  # DATA CHANGES TO 0xFF WHILE CLOCK IS STILL HIGH.
                    # ALWAYS MUST STAY 0xAA. If it changes to 0xFF, it's a latch!
*/

/* Test case:
In_3 In_2 In_1 Num_1 Out_0
0 0 0 4 0
0 0 1 5 1
0 0 0 210 0
0 0 1 253 1
0 1 1 65 0
0 1 0 102 1
0 1 1 237 1
0 1 0 179 0
1 0 0 102 1
1 0 0 0 1
1 0 0 252 0
1 0 1 179 1
1 0 1 0 1
1 0 1 112 0
1 1 0 0 1
1 1 0 243 1
1 1 0 123 1
1 1 1 0 0
1 1 1 243 0
1 1 1 123 0
*/

/* Test case:
C_2 C_1 C_0 A_0 B_0 O_0
0 0 1 9 6 15 #addition and subtraction
0 1 0 9 6 3
0 0 1 6 7 13
0 1 0 111 67 44
0 0 1 32 59 91
0 1 1 51 60 48  #and
0 1 1 3 2 2
0 1 1 5 3 1
0 1 1 12 25 8
0 1 1 4 8 0
1 0 1 5 3 7 #or
1 0 1 2 8 10
1 0 1 12 25 29
1 0 1 0 7 7
1 0 0 1 1 254 #nand
1 0 0 2 4 255
1 0 0 15 3 252
1 1 0 1 0 254 #nor
1 1 0 3 5 248
1 1 0 128 64 63
1 1 1 5 3 6 #xor
1 1 1 10 10 0
1 1 1 85 170 255
1 1 1 14 1 15
*/
